# Fritzing sketch Open_ID (saved by Fritzing 1.0.5)
circuit board: 8.46667cm x 5.64444cm
breadboards: 1

parts:
  Componente1 = Arduino Uno (Rev3)
  LED1 = smd LED [color="Green (560nm)" package="0805 [SMD]"]
  LED2 = smd LED [color="Red (633nm)" package="1206 [SMD]"]
  R1 = Resistor [tolerance=±5% resistance=220 package="0805 [SMD]"]
  Componente2 = RFID-RC522-v2
  J1 = Piezo Speaker
  R2 = Resistor [tolerance=±5% resistance=220 package="0805 [SMD]"]
  Componente3 = LCD1602-I2C
  J2 = Basic Servo

nets (from the schematic view):
  N1: Componente1.A4/SDA, Componente3.SDA
  N2: Componente1.A5/SCL, Componente3.SCL
  N3: Componente1.D8, J1.pin2
  N4: Componente1.D9_PWM, Componente2.RST
  N5: Componente1.D10_PWM/SS, Componente2.MOSI
  N6: Componente1.D11_PWM/MOSI, Componente2.SDA
  N7: Componente1.D12/MISO, Componente2.MISO
  N8: Componente1.D13/SCK, Componente2.SCK
  N9: Componente1.D3_PWM, J2.pulse
  N10: Componente1.D6_PWM, R2.Pin_1
  3V3: Componente1.3V3, Componente2.3.3V
  VCC: Componente1.5V, Componente3.VCC, J2.vcc
  GND: Componente1.GND, LED1.cathode, LED1.anode, LED2.anode, R1.Pin_0, Componente2.GND, J1.pin1, R2.Pin_0, Componente3.GND, J2.gnd

custom parts:
  RFID-RC522-v2: A simple China made RFID-RC522 Reader; do check the pin labels, as this is a MFRC522 based clone.
  LCD1602-I2C: A standard character display, usually with 2x16 characters. Comes in many colors with LCM1602 IIC attached.

// code stored in the sketch: Frit_Cod.ino
#include <SPI.h>
#include <MFRC522.h>
#include <Servo.h>
#include <LiquidCrystal.h>


#define SS_PIN 10
#define RST_PIN 9
MFRC522 mfrc522(SS_PIN, RST_PIN);

Servo servo;
int servoPin = 6;


int ledVerde = 4;
int ledRojo = 5;


int buzzer = 7;


LiquidCrystal lcd(8, 3, 2, A0, A1, A2);


String tarjetaPermitida = "A1 B2 C3 D4";

void setup() {
  Serial.begin(9600);
  SPI.begin();
  mfrc522.PCD_Init();

  servo.attach(servoPin);
  servo.write(0); 

  pinMode(ledVerde, OUTPUT);
  pinMode(ledRojo, OUTPUT);
  pinMode(buzzer, OUTPUT);

  lcd.begin(16, 2);
  lcd.print("Sistema RFID");
  delay(2000);
  lcd.clear();
}

void loop() {

  if (!mfrc522.PICC_IsNewCardPresent()) return;
  if (!mfrc522.PICC_ReadCardSerial()) return;

 
  String UID = "";
  for (byte i = 0; i < mfrc522.uid.size; i++) {
    UID.concat(String(mfrc522.uid.uidByte[i], HEX));
    if (i < mfrc522.uid.size - 1) UID.concat(" ");
  }
  UID.toUpperCase();

  Serial.print("UID detectado: ");
  Serial.println(UID);

  lcd.clear();

  if (UID == tarjetaPermitida) {
  
    digitalWrite(ledVerde, HIGH);
    tone(buzzer, 1000, 200);
    lcd.print("Acceso OK");
    servo.write(90); 

    delay(3000); 
    servo.write(0); 
    digitalWrite(ledVerde, LOW);
  } else {

    digitalWrite(ledRojo, HIGH);
    tone(buzzer, 500, 1000);
    lcd.print("Acceso DENEGADO");
    delay(2000);
    digitalWrite(ledRojo, LOW);
  }

  mfrc522.PICC_HaltA();
  mfrc522.PCD_StopCrypto1();
}
